// Logisim project RISCV32.circ as structural Verilog: 6 circuits, main circuit RISCV
module RISCV (
);

  wire and_1_out, and_2_out, and_3_out, and_4_out, and_5_out, and_6_out, clock_1_out,
       comparator_black_box_1_p3, comparator_black_box_1_p4, decodenoop_1_alusrc, decodenoop_1_branch,
       decodenoop_1_memread, decodenoop_1_memtoreg, decodenoop_1_memwrite, decodenoop_1_regwrite, not_1_out,
       or_1_out, xnor_1_out;
  wire [1:0] register_1_q_2;
  wire [2:0] risc_vprogramrom_1_p2_2;
  wire [3:0] genaluop_1_alucontrol, multiplexer_6_out, remaindertoonehot_1_onehot;
  wire [3:3] risc_vprogramrom_1_p2_3;
  wire [7:0] bitselector_1_out;
  wire [29:0] incrementer_1_p2, register_1_q;
  wire [31:0] alu_1_p5, bit_extender_1_out, bit_extender_2_out, immediategen_1_imm32, multiplexer_1_out,
       multiplexer_2_out, multiplexer_3_out, multiplexer_4_out, multiplexer_5_out, multiplexer_7_out,
       multiplexer_8_out, ram_1_p7, registerfile_1_p1, registerfile_1_p7, registerfile_1_p8;
  wire [31:1] risc_vprogramrom_1_p2;

  Clock clock_1 (.out(clock_1_out));
  Register #(.width(32)) register_1 (
    .D(multiplexer_3_out), .clk(clock_1_out), .Q({register_1_q, register_1_q_2}));  // open: en, clr
  // RISC_VProgramROM risc_vprogramrom_1: pin names not known; wires that end beside it: {register_1_q, register_1_q_2}, {risc_vprogramrom_1_p2[31:15], risc_vprogramrom_1_p2_2, risc_vprogramrom_1_p2[11:1], risc_vprogramrom_1_p2_3[3]}
  GenALUop genaluop_1 (
    .instr7({risc_vprogramrom_1_p2[6:1], risc_vprogramrom_1_p2_3[3]}), .instr_30(risc_vprogramrom_1_p2[30]),
    .func3(risc_vprogramrom_1_p2_2), .ALUcontrol(genaluop_1_alucontrol));
  ImmediateGen immediategen_1 (
    .instr32({risc_vprogramrom_1_p2[31:15], risc_vprogramrom_1_p2_2, risc_vprogramrom_1_p2[11:1], risc_vprogramrom_1_p2_3[3]}),
    .imm32(immediategen_1_imm32));
  decodeNoOp decodenoop_1 (
    .instr({risc_vprogramrom_1_p2[6:1], risc_vprogramrom_1_p2_3[3]}), .ALUsrc(decodenoop_1_alusrc),
    .MemToReg(decodenoop_1_memtoreg), .RegWrite(decodenoop_1_regwrite), .MemRead(decodenoop_1_memread),
    .MemWrite(decodenoop_1_memwrite), .branch(decodenoop_1_branch));
  and and_1 (and_1_out, ~decodenoop_1_memtoreg, decodenoop_1_regwrite);  // AND_Gate
  and and_2 (and_2_out, decodenoop_1_memtoreg, decodenoop_1_regwrite, xnor_1_out);
  or or_1 (or_1_out, and_1_out, and_2_out);
  // Incrementer #(.width(30)) incrementer_1: pin names not known; wires that end beside it: register_1_q, incrementer_1_p2
  // RegisterFile registerfile_1: pin names not known; wires that end beside it: registerfile_1_p1, clock_1_out, or_1_out, risc_vprogramrom_1_p2[11:7], risc_vprogramrom_1_p2[19:15], risc_vprogramrom_1_p2[24:20], registerfile_1_p7, registerfile_1_p8
  Multiplexer #(.width(32)) multiplexer_1 (
    .in0(registerfile_1_p7), .in1({register_1_q, register_1_q_2}), .out(multiplexer_1_out),
    .sel(decodenoop_1_branch));
  Multiplexer #(.width(32)) multiplexer_2 (
    .in0(registerfile_1_p8), .in1(immediategen_1_imm32), .out(multiplexer_2_out), .sel(decodenoop_1_alusrc));
  not not_1 (not_1_out, risc_vprogramrom_1_p2_2[2]);
  and and_3 (and_3_out, risc_vprogramrom_1_p2[4], not_1_out, risc_vprogramrom_1_p2_2[1]);
  // Comparator_Black_Box comparator_black_box_1: pin names not known; wires that end beside it: registerfile_1_p7, registerfile_1_p8, comparator_black_box_1_p3, comparator_black_box_1_p4
  // ALU alu_1: pin names not known; wires that end beside it: multiplexer_1_out, multiplexer_2_out, genaluop_1_alucontrol, multiplexer_2_out[4:0], alu_1_p5
  Multiplexer #(.width(32)) multiplexer_3 (
    .in0({incrementer_1_p2, register_1_q_2}), .in1(alu_1_p5), .out(multiplexer_3_out), .sel(and_4_out));
  and and_4 (and_4_out, decodenoop_1_branch, comparator_black_box_1_p3);
  assign bit_extender_1_out = {{31{1'b0}}, comparator_black_box_1_p4};  // Bit_Extender bit_extender_1
  Multiplexer #(.width(32)) multiplexer_4 (
    .in0(alu_1_p5), .in1(immediategen_1_imm32), .out(multiplexer_4_out), .sel(risc_vprogramrom_1_p2[2]));
  remainderToOneHot remaindertoonehot_1 (.remainder(multiplexer_4_out[1:0]), .oneHot(remaindertoonehot_1_onehot));
  Multiplexer #(.width(32)) multiplexer_5 (
    .in0({registerfile_1_p8[7:0], registerfile_1_p8[7:0], registerfile_1_p8[7:0], registerfile_1_p8[7:0]}),
    .in1(registerfile_1_p8), .out(multiplexer_5_out), .sel(risc_vprogramrom_1_p2_2[1]));
  and and_5 (and_5_out, decodenoop_1_memwrite, xnor_1_out);
  NotExactlyOne xnor_1 (
    .out(xnor_1_out), .in0(multiplexer_4_out[22]), .in1(multiplexer_4_out[23]), .in2(multiplexer_4_out[24]),
    .in3(multiplexer_4_out[25]), .in4(multiplexer_4_out[26]), .in5(multiplexer_4_out[27]),
    .in6(multiplexer_4_out[28]), .in7(multiplexer_4_out[29]), .in8(multiplexer_4_out[30]),
    .in9(multiplexer_4_out[31]));
  Multiplexer #(.width(4)) multiplexer_6 (
    .in0(remaindertoonehot_1_onehot), .in1({4{risc_vprogramrom_1_p2_3[3]}}), .out(multiplexer_6_out),
    .sel(risc_vprogramrom_1_p2_2[1]));
  and and_6 (and_6_out, decodenoop_1_memread, xnor_1_out);
  // RAM ram_1: pin names not known; wires that end beside it: multiplexer_4_out[21:2], multiplexer_5_out, and_5_out, multiplexer_6_out, clock_1_out, and_6_out, ram_1_p7
  BitSelector #(.group(8), .width(32)) bitselector_1 (
    .in(ram_1_p7), .out(bitselector_1_out), .sel(multiplexer_4_out[1:0]));
  assign bit_extender_2_out = {{24{1'b0}}, bitselector_1_out};  // Bit_Extender bit_extender_2
  Multiplexer #(.width(32)) multiplexer_7 (
    .in0(bit_extender_2_out), .in1(ram_1_p7), .out(multiplexer_7_out), .sel(risc_vprogramrom_1_p2_2[1]));
  Multiplexer #(.width(32)) multiplexer_8 (
    .in0(multiplexer_4_out), .in1(bit_extender_1_out), .out(multiplexer_8_out), .sel(and_3_out));
  Multiplexer #(.width(32)) multiplexer_9 (
    .in0(multiplexer_8_out), .in1(multiplexer_7_out), .out(registerfile_1_p1), .sel(decodenoop_1_memtoreg));

  // Notes on the sheet:
  //   controls the mux which lets values from the comparator go to rd
  //   increment PC by 4
  //   ensure write enable off 
  //   when address over upper bound
  //   chooses the cs value for RAM
  //   for correct lb and lw
  //   10 MSBs All zero
  //   chooses between PC+branch or PC+4
  //   for correct sb and sw
  //   take comparator or ALU result to register
  //   take RAM output or ALU/comparator output to rd
endmodule

module decodeNoOp (
  input  [6:0] instr,
  output ALUsrc,
  output MemToReg,
  output RegWrite,
  output MemRead,
  output MemWrite,
  output branch
);

  wire not_1_out, not_2_out;

  not not_1 (not_1_out, instr[6]);
  not not_2 (not_2_out, instr[5]);
  not not_3 (MemToReg, instr[4]);
  or or_1 (ALUsrc, not_2_out, MemToReg, instr[2]);
  or or_2 (RegWrite, not_2_out, instr[4]);
  and and_1 (MemRead, not_2_out, MemToReg);
  and and_2 (MemWrite, not_1_out, instr[5], MemToReg);

  assign branch = instr[6];
endmodule

module ImmediateGen (
  input  [31:0] instr32,
  output [31:0] imm32
);

  wire and_1_out, not_1_out;
  wire [1:0] or_2_out;
  wire [11:0] bit_extender_3_out;
  wire [31:0] bit_extender_1_out, bit_extender_2_out, bit_extender_4_out;

  assign bit_extender_1_out = {{20{instr32[31]}}, instr32[31:20]};  // Bit_Extender bit_extender_1
  not not_1 (not_1_out, instr32[2]);
  assign bit_extender_2_out = {{20{instr32[31]}}, {instr32[31:25], instr32[11:7]}};  // Bit_Extender bit_extender_2
  assign bit_extender_3_out = {{11{1'b0}}, instr32[3]};  // Bit_Extender bit_extender_3
  assign bit_extender_4_out = {{19{instr32[31]}}, {instr32[31:25], instr32[11:7], instr32[3]}};  // Bit_Extender bit_extender_4
  or or_1 (or_2_out[1], instr32[2], instr32[6]);
  and and_1 (and_1_out, instr32[5], not_1_out);
  or or_2 (or_2_out[0], and_1_out, instr32[6]);
  Multiplexer #(.select(2), .width(32)) multiplexer_1 (
    .in0(bit_extender_1_out), .in1(bit_extender_2_out), .in2({instr32[31:12], bit_extender_3_out}),
    .in3(bit_extender_4_out), .out(imm32), .sel(or_2_out));

  // Notes on the sheet:
  //   sign extend for SB SW
  //   sign extend for ADDI ANDI LW LB
  //   shift left 1 for BEQ
  //   shift left 12 for LUI
endmodule

module GenALUop (
  input  [6:0] instr7,
  input  instr_30,
  input  [2:0] func3,
  output [3:0] ALUcontrol
);

  wire and_2_out, and_3_out, and_4_out, and_5_out, and_6_out, not_1_out, not_2_out, not_3_out;

  not not_1 (not_1_out, instr7[6]);
  not not_2 (not_2_out, instr7[5]);
  not not_3 (not_3_out, instr7[2]);
  and and_1 (ALUcontrol[3], instr7[4], not_3_out, func3[1]);
  and and_2 (and_2_out, not_2_out, func3[0]);
  and and_3 (and_3_out, not_1_out, not_3_out, func3[2]);
  and and_4 (and_4_out, instr7[5], instr7[4], not_3_out, instr_30);
  and and_5 (and_5_out, not_1_out, func3[0]);
  and and_6 (and_6_out, instr7[4], func3[2]);
  or or_1 (ALUcontrol[2], and_2_out, and_3_out, and_4_out);
  or or_2 (ALUcontrol[1], and_5_out, instr7[2], and_6_out);

  assign ALUcontrol[0] = instr7[1];
endmodule

module comparator_to_reg (
  input  [6:0] instr,
  input  [2:0] func3,
  output bboxToReg
);

  wire not_1_out;

  not not_1 (not_1_out, func3[2]);
  and and_1 (bboxToReg, instr[4], not_1_out, func3[1]);

  // Notes on the sheet:
  //   This subcircuit was used to make a part that I pasted into the actual RISCV circuit
endmodule

module remainderToOneHot (
  input  [1:0] remainder,
  output [3:0] oneHot
);

  wire not_1_out, not_2_out;

  not not_1 (not_1_out, remainder[1]);
  not not_2 (not_2_out, remainder[0]);
  and and_1 (oneHot[3], remainder[1], remainder[0]);
  and and_2 (oneHot[2], remainder[1], not_2_out);
  and and_3 (oneHot[1], not_1_out, remainder[0]);
  and and_4 (oneHot[0], not_1_out, not_2_out);
endmodule
