// Logisim project ALU_template_BRL.circ as structural Verilog: 13 circuits, main circuit LeftShift32
module LeftShift32 (
  input  Cin,
  input  [31:0] B,
  input  [4:0] Sa,
  output [31:0] C
);

  wire [31:0] leftshift1_1_out_3, leftshift2_1_out_3, leftshift4_1_out_3, leftshift8_1_out_3,
       leftshift16_1_out_3, multiplexer_1_out, multiplexer_2_out, multiplexer_3_out, multiplexer_4_out;

  leftshift16 leftshift16_1 (.cin(Cin), .B(B), .out_3(leftshift16_1_out_3));
  Multiplexer #(.width(32)) multiplexer_1 (.in0(B), .in1(leftshift16_1_out_3), .out(multiplexer_1_out), .sel(Sa[4]));
  leftshift8 leftshift8_1 (.cin(Cin), .B(multiplexer_1_out), .out_3(leftshift8_1_out_3));
  Multiplexer #(.width(32)) multiplexer_2 (
    .in0(multiplexer_1_out), .in1(leftshift8_1_out_3), .out(multiplexer_2_out), .sel(Sa[3]));
  Multiplexer #(.width(32)) multiplexer_3 (
    .in0(multiplexer_2_out), .in1(leftshift4_1_out_3), .out(multiplexer_3_out), .sel(Sa[2]));
  leftshift4 leftshift4_1 (.cin(Cin), .b(multiplexer_2_out), .out_3(leftshift4_1_out_3));
  leftshift2 leftshift2_1 (.cin(Cin), .b(multiplexer_3_out), .out_3(leftshift2_1_out_3));
  Multiplexer #(.width(32)) multiplexer_4 (
    .in0(multiplexer_3_out), .in1(leftshift2_1_out_3), .out(multiplexer_4_out), .sel(Sa[1]));
  leftshift1 leftshift1_1 (.cin(Cin), .B(multiplexer_4_out), .out_3(leftshift1_1_out_3));
  Multiplexer #(.width(32)) multiplexer_5 (.in0(multiplexer_4_out), .in1(leftshift1_1_out_3), .out(C), .sel(Sa[0]));

  // Notes on the sheet:
  //   Do not delete or rename any of the input or output pins, and do not add any other pins
  //   (You are free to move the pins around however)
endmodule

module Add32 (
  input  [31:0] A,
  input  Cin,
  input  [31:0] B,
  output V,
  output [31:0] C
);

  wire add8_1_cout, add8_2_cout, add8_3_cout;

  Add8 add8_1 (.A(A[7:0]), .Cin(Cin), .B(B[7:0]), .Cout(add8_1_cout), .S(C[7:0]));  // open: V
  Add8 add8_2 (.A(A[15:8]), .Cin(add8_1_cout), .B(B[15:8]), .Cout(add8_2_cout), .S(C[15:8]));  // open: V
  Add8 add8_3 (.A(A[23:16]), .Cin(add8_2_cout), .B(B[23:16]), .Cout(add8_3_cout), .S(C[23:16]));  // open: V
  Add8 add8_4 (.A(A[31:24]), .Cin(add8_3_cout), .B(B[31:24]), .V(V), .S(C[31:24]));  // open: Cout

  // Notes on the sheet:
  //   (You are free to move the pins around however)
  //   Do not delete or rename any of the input or output pins, and do not add any other pins
endmodule

module ALU32 (
  input  [31:0] A,
  input  [31:0] B,
  input  [3:0] Op,
  input  [4:0] Sa,
  output [31:0] C,
  output V
);

  wire add32_1_v, and_2_out, and_3_out, isallzeros_1_onebitoutput, nand_1_out, not_2_out, xnor_1_out;
  wire [31:0] add32_1_c, and_1_out, bit_extender_1_out, bit_extender_2_out, bit_extender_3_out,
       multiplexer_1_out, multiplexer_2_out, multiplexer_3_out, multiplexer_4_out, multiplexer_5_out,
       multiplexer_6_out, multiplexer_7_out, nand_2_out, not_1_out, or_1_out, shift32_1_c, xor_1_out;

  assign and_1_out = A & B;  // AND_Gate and_1, 32 bits wide
  assign or_1_out = A | B;  // OR_Gate or_1, 32 bits wide
  nand nand_1 (nand_1_out, Op[1], Op[0]);
  assign not_1_out = ~B;  // NOT_Gate not_1, 32 bits wide
  and and_2 (and_2_out, Op[1], Op[0]);
  and and_3 (and_3_out, ~Op[3], Op[1], B[31]);  // AND_Gate
  assign xor_1_out = A ^ B;  // XOR_Gate xor_1, 32 bits wide
  not not_2 (not_2_out, A[31]);
  assign nand_2_out = ~(A & B);  // NAND_Gate nand_2, 32 bits wide
  Multiplexer #(.width(32)) multiplexer_1 (.in0(and_1_out), .in1(or_1_out), .out(multiplexer_1_out), .sel(Op[0]));
  Multiplexer #(.width(32)) multiplexer_2 (.in0(not_1_out), .in1(B), .out(multiplexer_2_out), .sel(and_2_out));
  assign bit_extender_1_out = {{31{1'b0}}, not_2_out};  // Bit_Extender bit_extender_1
  assign bit_extender_2_out = {{31{1'b0}}, A[31]};  // Bit_Extender bit_extender_2
  Multiplexer #(.width(32)) multiplexer_3 (
    .in0(bit_extender_1_out), .in1(xor_1_out), .out(multiplexer_3_out), .sel(Op[0]));
  Multiplexer #(.width(32)) multiplexer_4 (
    .in0(bit_extender_2_out), .in1(nand_2_out), .out(multiplexer_4_out), .sel(Op[0]));
  Shift32 shift32_1 (.Cin(and_3_out), .B(B), .Sa(Sa), .SL(Op[2]), .C(shift32_1_c));
  IsAllZeros isallzeros_1 (.B(add32_1_c), .onebitOutput(isallzeros_1_onebitoutput));
  Add32 add32_1 (.A(A), .Cin(nand_1_out), .B(multiplexer_2_out), .V(add32_1_v), .C(add32_1_c));
  xnor xnor_1 (xnor_1_out, isallzeros_1_onebitoutput, Op[0]);
  Multiplexer #(.width(32)) multiplexer_5 (
    .in0(multiplexer_1_out), .in1(add32_1_c), .out(multiplexer_5_out), .sel(Op[1]));
  Multiplexer #(.width(32)) multiplexer_6 (
    .in0(bit_extender_3_out), .in1(shift32_1_c), .out(multiplexer_6_out), .sel(Op[1]));
  assign bit_extender_3_out = {{31{1'b0}}, xnor_1_out};  // Bit_Extender bit_extender_3
  Multiplexer #(.width(32)) multiplexer_7 (
    .in0(multiplexer_3_out), .in1(multiplexer_4_out), .out(multiplexer_7_out), .sel(Op[1]));
  and and_4 (V, add32_1_v, Op[1], ~Op[2], ~Op[3]);  // AND_Gate
  Multiplexer #(.select(2), .width(32)) multiplexer_8 (
    .in0(multiplexer_5_out), .in1(shift32_1_c), .in2(multiplexer_6_out), .in3(multiplexer_7_out), .out(C),
    .sel(Op[3:2]));

  // Notes on the sheet:
  //   for the NAND gate to the right:
  //   output=1 when at least 1 of the 2 LSBs = 0 
  //   ensures Cin=0 only for op=011x
  //   filters on LSB
  //   signal is 1 when 2LSBs are both 1
  //   filters on LSB
  //   filters on LSB
  //   filters on the 2nd LSB
  //   filters on the 2nd LSB
  //   filters on the 2nd LSB
  //   filters based on 2 MSBs of Op
  //   Do not delete or rename any of the input or output pins, and do not add any other pins
  //   (You are free to move the pins around however)
endmodule

module Shift32 (
  input  Cin,
  input  [31:0] B,
  input  [4:0] Sa,
  input  SL,
  output [31:0] C
);

  wire [31:0] leftshift32_1_c, multiplexer_1_out;

  Multiplexer #(.width(32)) multiplexer_1 (
    .in0(B),
    .in1({B[0], B[1], B[2], B[3], B[4], B[5], B[6], B[7], B[8], B[9], B[10], B[11], B[12], B[13], B[14], B[15], B[16], B[17], B[18], B[19], B[20], B[21], B[22], B[23], B[24], B[25], B[26], B[27], B[28], B[29], B[30], B[31]}),
    .out(multiplexer_1_out), .sel(SL));
  LeftShift32 leftshift32_1 (.Cin(Cin), .B(multiplexer_1_out), .Sa(Sa), .C(leftshift32_1_c));
  Multiplexer #(.width(32)) multiplexer_2 (
    .in0(leftshift32_1_c),
    .in1({leftshift32_1_c[0], leftshift32_1_c[1], leftshift32_1_c[2], leftshift32_1_c[3], leftshift32_1_c[4], leftshift32_1_c[5], leftshift32_1_c[6], leftshift32_1_c[7], leftshift32_1_c[8], leftshift32_1_c[9], leftshift32_1_c[10], leftshift32_1_c[11], leftshift32_1_c[12], leftshift32_1_c[13], leftshift32_1_c[14], leftshift32_1_c[15], leftshift32_1_c[16], leftshift32_1_c[17], leftshift32_1_c[18], leftshift32_1_c[19], leftshift32_1_c[20], leftshift32_1_c[21], leftshift32_1_c[22], leftshift32_1_c[23], leftshift32_1_c[24], leftshift32_1_c[25], leftshift32_1_c[26], leftshift32_1_c[27], leftshift32_1_c[28], leftshift32_1_c[29], leftshift32_1_c[30], leftshift32_1_c[31]}),
    .out(C), .sel(SL));

  // Notes on the sheet:
  //   Do not delete or rename any of the input or output pins, and do not add any other pins
  //   (You are free to move the pins around however)
endmodule

module Add4 (
  input  [3:0] A,
  input  Cin,
  input  [3:0] B,
  output Cout,
  output V,
  output [3:0] S
);

  wire add1_1_cout, add1_2_cout, add1_3_cout;

  Add1 add1_1 (.A(A[0]), .B(B[0]), .C_in(Cin), .S(S[0]), .Cout(add1_1_cout));
  Add1 add1_2 (.A(A[1]), .B(B[1]), .C_in(add1_1_cout), .S(S[1]), .Cout(add1_2_cout));
  Add1 add1_3 (.A(A[2]), .B(B[2]), .C_in(add1_2_cout), .S(S[2]), .Cout(add1_3_cout));
  Add1 add1_4 (.A(A[3]), .B(B[3]), .C_in(add1_3_cout), .S(S[3]), .Cout(Cout));
  xor xor_1 (V, Cout, add1_3_cout);
endmodule

module Add1 (
  input  A,
  input  B,
  input  C_in,
  output S,
  output Cout
);

  wire and_1_out, and_2_out, xor_1_out;

  xor xor_1 (xor_1_out, A, B);
  xor xor_2 (S, xor_1_out, C_in);
  and and_1 (and_1_out, xor_1_out, C_in);
  and and_2 (and_2_out, A, B);
  or or_1 (Cout, and_1_out, and_2_out);
endmodule

module Add8 (
  input  [7:0] A,
  input  Cin,
  input  [7:0] B,
  output Cout,
  output V,
  output [7:0] S
);

  wire add4_1_cout;

  Add4 add4_1 (.A(A[3:0]), .Cin(Cin), .B(B[3:0]), .Cout(add4_1_cout), .S(S[3:0]));  // open: V
  Add4 add4_2 (.A(A[7:4]), .Cin(add4_1_cout), .B(B[7:4]), .Cout(Cout), .V(V), .S(S[7:4]));
endmodule

module IsAllZeros (
  input  [31:0] B,
  output onebitOutput
);

  nor nor_1 (onebitOutput, B[0], B[1], B[2], B[3], B[4], B[5], B[6], B[7], B[8], B[9], B[10], B[11], B[12], B[13], B[14], B[15], B[17], B[18], B[19], B[20], B[21], B[22], B[23], B[24], B[25], B[26], B[27], B[28], B[29], B[30], B[31]);
endmodule

module leftshift1 (
  input  cin,
  input  [31:0] B,
  output [31:0] out_3
);


  assign out_3 = {B[30:0], cin};
endmodule

module leftshift2 (
  input  cin,
  input  [31:0] b,
  output [31:0] out_3
);

  wire [31:0] leftshift1_1_out_3;

  leftshift1 leftshift1_1 (.cin(cin), .B(b), .out_3(leftshift1_1_out_3));
  leftshift1 leftshift1_2 (.cin(cin), .B(leftshift1_1_out_3), .out_3(out_3));
endmodule

module leftshift4 (
  input  cin,
  input  [31:0] b,
  output [31:0] out_3
);

  wire [31:0] leftshift2_1_out_3;

  leftshift2 leftshift2_1 (.cin(cin), .b(b), .out_3(leftshift2_1_out_3));
  leftshift2 leftshift2_2 (.cin(cin), .b(leftshift2_1_out_3), .out_3(out_3));
endmodule

module leftshift8 (
  input  cin,
  input  [31:0] B,
  output [31:0] out_3
);

  wire [31:0] leftshift4_1_out_3;

  leftshift4 leftshift4_1 (.cin(cin), .b(B), .out_3(leftshift4_1_out_3));
  leftshift4 leftshift4_2 (.cin(cin), .b(leftshift4_1_out_3), .out_3(out_3));
endmodule

module leftshift16 (
  input  cin,
  input  [31:0] B,
  output [31:0] out_3
);

  wire [31:0] leftshift8_1_out_3;

  leftshift8 leftshift8_1 (.cin(cin), .B(B), .out_3(leftshift8_1_out_3));
  leftshift8 leftshift8_2 (.cin(cin), .B(leftshift8_1_out_3), .out_3(out_3));
endmodule
